// Logisim project four.circ as structural Verilog
module a (
  input  A,
  input  B,
  input  C,
  input  D,
  output F
);

  wire n74157_1_p1;

  // _74157 74157_1: pin names not known; wires that end beside it: n74157_1_p1, 1'b1, 1'b0, D, 1'b1, 1'b0, n74157_1_p1, 1'b0, 1'b1, 1'b0
  // _74151 74151_1: pin names not known; wires that end beside it: n74157_1_p1, 1'b0, n74157_1_p1, 1'b1, F, 1'b0, 1'b0, 1'b1, 1'b0, D, 1'b0, D, C, B, A

  // Notes on the sheet:
  //   F = SUMMATION(0, 1, 2, 6, 11, 15)
endmodule

module b (
  input  A,
  input  B,
  input  C,
  input  D,
  output F
);

  wire n74153_1_p7, n74153_1_p16, n74157_1_p6, n74157_2_p5;

  // _74157 74157_1: pin names not known; wires that end beside it: 1'b1, 1'b0, D, 1'b1, 1'b0, n74157_1_p6, 1'b1, 1'b0
  // _74157 74157_2: pin names not known; wires that end beside it: 1'b1, A, 1'b1, 1'b0, n74157_2_p5, 1'b0, 1'b1, 1'b0
  // _74153 74153_1: pin names not known; wires that end beside it: A, B, D, n74157_1_p6, n74157_1_p6, 1'b0, n74153_1_p7, 1'b0, 1'b1, n74157_2_p5, C, D, 1'b1, n74157_1_p6, 1'b1, n74153_1_p16
  // _74153 74153_2: pin names not known; wires that end beside it: 1'b0, n74153_1_p7, 1'b1, 1'b1, 1'b1, 1'b0, F, 1'b0, 1'b1, n74153_1_p16

  // Notes on the sheet:
  //   F = PRODUCT(0, 1, 3, 5, 6, 11, 14)
endmodule

module c (
  input  CLEAR,
  input  PRESET,
  output Y2,
  output Y1,
  output Y0
);

  wire clock_1_out;

  Clock clock_1 (.out(clock_1_out));
  // _7476 7476_1: pin names not known; wires that end beside it: clock_1_out, CLEAR, 1'b1, 1'b1, clock_1_out, PRESET, Y0, Y2, 1'b0, 1'b1, Y1, 1'b1
  // _7476 7476_2: pin names not known; wires that end beside it: clock_1_out, PRESET, Y1, 1'b1, Y1, Y0, 1'b0
endmodule

module d (
  input  CLEAR,
  input  PRESET,
  input  D,
  input  J,
  input  K,
  output Q,
  output Q_2
);

  wire clock_1_out;

  Clock clock_1 (.out(clock_1_out));
  // _7474 7474_1: pin names not known; wires that end beside it: CLEAR, D, clock_1_out, PRESET, Q, 1'b0, 1'b1
  // _7476 7476_1: pin names not known; wires that end beside it: clock_1_out, PRESET, CLEAR, J, 1'b1, K, Q_2, 1'b0
endmodule
