// Logisim project one.circ as structural Verilog: 3 circuits, main circuit main
module main (
  input  X,
  input  Y,
  output XOR,
  output Ding
);

  wire and_1_out, and_2_out, and_3_out, not_1_out, not_2_out;

  not not_1 (not_1_out, X);
  not not_2 (not_2_out, Y);
  and and_1 (and_1_out, X, Y);
  and and_2 (and_2_out, Y, not_1_out);
  and and_3 (and_3_out, not_2_out, X);
  or or_1 (Ding, and_1_out, X);
  or or_2 (XOR, and_2_out, and_3_out);
endmodule

module one (
  input  A,
  input  B,
  input  C,
  input  D,
  output F
);

  wire and_1_out, and_2_out, not_1_out, not_2_out, not_3_out, or_1_out;

  not not_1 (not_1_out, A);
  and and_1 (and_1_out, not_1_out, D);
  and and_2 (and_2_out, B, C);
  or or_1 (or_1_out, C, D);
  not not_2 (not_2_out, and_2_out);
  not not_3 (not_3_out, or_1_out);
  or or_2 (F, A, and_1_out, not_2_out, not_3_out);

  // Notes on the sheet:
  //   F(A,B,C,D) = A + (BC)' + DA' + (C+D)'
endmodule

module two (
  input  A,
  input  B,
  input  C,
  input  D,
  output out_5
);

  wire And_p6, Not_p1, Not_p2, Not_p4, Not_p5, Not_p6, Or_p3, Or_p6;

  // _7404 Not: pin names not known; wires that end beside it: Not_p1, Not_p2, A, Not_p4, Not_p5, Not_p6
  // _7408 And: pin names not known; wires that end beside it: C, B, Not_p1, Not_p4, D, And_p6
  // _7432 Or: pin names not known; wires that end beside it: Not_p6, And_p6, Or_p3, A, Not_p2, Or_p6, Or_p3, Or_p6, out_5, D, C, Not_p5
endmodule
