// Logisim project three.circ as structural Verilog: 2 circuits, main circuit main
module main (
  input  A3,
  input  A2,
  input  A1,
  input  A0,
  output out_5
);

  wire n74138_1_p9, n74138_1_p10, n74138_1_p11, n74138_2_p9;

  // _74138 74138_1: pin names not known; wires that end beside it: A0, A1, A2, A3, 1'b0, 1'b1, 1'b0, 1'b1, n74138_1_p9, n74138_1_p10, n74138_1_p11
  // _74138 74138_2: pin names not known; wires that end beside it: A0, A1, A2, 1'b0, 1'b0, A3, 1'b0, 1'b1, n74138_2_p9
  // _7420 7420_1: pin names not known; wires that end beside it: n74138_1_p9, n74138_1_p10, n74138_1_p11, n74138_2_p9, out_5, 1'b0, 1'b1

  // Notes on the sheet:
  //   Implementation of a function F by 2 3*8 Decoder
  //   F = Summation(3, 4, 5, 9)
endmodule

module a (
  input  A3,
  input  A2,
  input  A1,
  input  A0,
  output out_5
);

  wire n7408_1_p3, n7408_1_p6, n7408_1_p10, n74138_1_p9, n74138_1_p10, n74138_1_p11, n74138_2_p9,
       n74138_2_p10;

  // _74138 74138_1: pin names not known; wires that end beside it: A0, A1, A2, A3, 1'b0, 1'b1, 1'b0, 1'b1, n74138_1_p9, n74138_1_p10, n74138_1_p11
  // _74138 74138_2: pin names not known; wires that end beside it: A0, A1, A2, 1'b0, 1'b0, A3, 1'b0, 1'b1, n74138_2_p9, n74138_2_p10
  // _7408 7408_1: pin names not known; wires that end beside it: n74138_1_p9, n74138_1_p10, n7408_1_p3, n7408_1_p3, n74138_1_p11, n7408_1_p6, 1'b0, 1'b1, n74138_2_p10, n7408_1_p10, out_5, n74138_2_p9, n7408_1_p6, n7408_1_p10

  // Notes on the sheet:
  //   F = Product(3,,4 5, 10, 11)
endmodule
