// Logisim project two.circ as structural Verilog
module a (
  input  A,
  input  B,
  input  C,
  input  D,
  output F
);

  wire and_1_out, and_2_out, and_3_out, not_1_out, not_2_out, not_3_out, or_1_out;

  not not_1 (not_1_out, A);
  not not_2 (not_2_out, B);
  not not_3 (not_3_out, D);
  or or_1 (or_1_out, not_2_out, C);
  and and_1 (and_1_out, not_1_out, not_3_out, not_3_out, or_1_out);
  and and_2 (and_2_out, A, B, D);
  and and_3 (and_3_out, A, C, D);
  or or_2 (F, and_1_out, and_2_out, and_3_out);

  // Notes on the sheet:
  //   F = A'D'(B' + C) + ABD + ACD
endmodule

module b (
  input  A,
  input  B,
  input  C,
  input  D,
  output F
);

  wire and_1_out, and_2_out, and_3_out, not_1_out, not_2_out, not_3_out, or_1_out;

  not not_1 (not_1_out, A);
  not not_2 (not_2_out, C);
  not not_3 (not_3_out, D);
  or or_1 (or_1_out, B, C);
  and and_1 (and_1_out, or_1_out, A, D);
  and and_2 (and_2_out, not_1_out, not_2_out, not_3_out);
  and and_3 (and_3_out, not_1_out, B, not_3_out);
  or or_2 (F, and_1_out, and_2_out, and_3_out);

  // Notes on the sheet:
  //   F = AD(B+C) + A'C'D' + A'BD'
endmodule

module c (
  input  A,
  input  B,
  input  C,
  input  D,
  output F
);

  wire And_p3, And_p6, And_p11, And_p14, n7404_1_p2, n7404_1_p4, n7404_1_p5, n7404_1_p8, n7408_1_p3,
       n7408_1_p5, n7408_1_p6, n7432_1_p11;

  // _7404 7404_1: pin names not known; wires that end beside it: 1'b0, n7404_1_p2, D, n7404_1_p4, n7404_1_p5, C, B, n7404_1_p8, A, 1'b1, n7404_1_p4, n7404_1_p2
  // _7408 And: pin names not known; wires that end beside it: n7404_1_p8, n7404_1_p4, And_p3, And_p3, D, And_p6, 1'b0, 1'b1, A, n7404_1_p4, And_p11, And_p11, n7404_1_p2, And_p14
  // _7408 7408_1: pin names not known; wires that end beside it: A, n7404_1_p5, n7408_1_p3, n7408_1_p3, n7408_1_p5, n7408_1_p6, 1'b1
  // _7432 7432_1: pin names not known; wires that end beside it: C, n7404_1_p4, D, n7404_1_p2, 1'b0, n7404_1_p2, n7404_1_p4, n7408_1_p5, n7408_1_p6, And_p6, n7432_1_p11, 1'b0, 1'b1, And_p14, n7432_1_p11, F
endmodule

module d (
  input  A,
  input  B,
  input  C,
  input  D,
  output F
);

  wire n7404_1_p4, n7404_1_p6, n7408_1_p3, n7408_1_p6, n7408_1_p11, n7408_1_p14, n7408_2_p3, n7408_2_p5,
       n7408_2_p6, n7432_1_p8;

  // _7404 7404_1: pin names not known; wires that end beside it: 1'b0, 1'b1, 1'b0, n7404_1_p4, C, n7404_1_p6, A, 1'b1, n7404_1_p6, n7404_1_p4
  // _7408 7408_1: pin names not known; wires that end beside it: n7404_1_p6, B, n7408_1_p3, n7408_1_p3, n7404_1_p4, n7408_1_p6, 1'b0, 1'b1, A, B, n7408_1_p11, n7408_1_p11, D, n7408_1_p14
  // _7408 7408_2: pin names not known; wires that end beside it: A, C, n7408_2_p3, n7408_2_p3, n7408_2_p5, n7408_2_p6, 1'b0, 1'b1
  // _7432 7432_1: pin names not known; wires that end beside it: n7404_1_p4, D, B, D, n7408_2_p5, n7408_2_p6, n7408_1_p6, n7432_1_p8, 1'b0, 1'b1, n7408_1_p14, n7432_1_p8, F
endmodule

module e (
  input  A,
  input  B,
  input  C,
  input  D,
  output F
);

  wire n7404_1_p4, n7404_1_p6, n7408_1_p3, n7408_1_p6, n7408_2_p3, n7408_2_p5, n7408_2_p6, n7408_2_p11,
       n7408_2_p14, n7432_1_p8;

  // _7404 7404_1: pin names not known; wires that end beside it: 1'b0, 1'b1, 1'b0, n7404_1_p4, C, n7404_1_p6, A, 1'b1, n7404_1_p6, n7404_1_p4
  // _7408 7408_1: pin names not known; wires that end beside it: A, C, n7408_1_p3, n7408_1_p3, D, n7408_1_p6, 1'b0, 1'b1
  // _7408 7408_2: pin names not known; wires that end beside it: n7404_1_p6, B, n7408_2_p3, n7408_2_p3, n7408_2_p5, n7408_2_p6, 1'b0, 1'b1, A, B, n7408_2_p11, n7408_2_p11, C, n7408_2_p14
  // _7432 7432_1: pin names not known; wires that end beside it: n7404_1_p4, D, n7404_1_p4, D, n7408_2_p5, n7408_2_p6, n7408_1_p6, n7432_1_p8, 1'b0, 1'b1, n7408_2_p14, n7432_1_p8, F
endmodule
