// Logisim project offline.circ as structural Verilog: 3 circuits, main circuit main
module main (
  input  Serial_Input_for_Right_Shift,
  input  I3,
  input  I2,
  input  I1,
  input  I0,
  input  Serial_Input_for_Left_Shift,
  input  [1:0] in_7,
  output A3,
  output A2,
  output A1,
  output A0
);

  wire button_1_out, clock_1_out, multiplexer_1_out, multiplexer_2_out, multiplexer_3_out, multiplexer_4_out;

  Multiplexer #(.select(2)) multiplexer_1 (
    .in0(A3), .in1(Serial_Input_for_Right_Shift), .in2(A2), .in3(I3), .out(multiplexer_1_out), .sel(in_7));  // open: en
  Multiplexer #(.select(2)) multiplexer_2 (
    .in0(A2), .in1(A3), .in2(A1), .in3(I2), .out(multiplexer_2_out), .sel(in_7));  // open: en
  Multiplexer #(.select(2)) multiplexer_3 (
    .in0(A1), .in1(A2), .in2(A0), .in3(I1), .out(multiplexer_3_out), .sel(in_7));  // open: en
  Multiplexer #(.select(2)) multiplexer_4 (
    .in0(A0), .in1(A1), .in2(Serial_Input_for_Left_Shift), .in3(I0), .out(multiplexer_4_out), .sel(in_7));  // open: en
  Clock clock_1 (.out(clock_1_out));
  Button button_1 (.out(button_1_out));
  D_Flip_Flop #(.trigger("falling")) d_ff_1 (
    .clk(clock_1_out), .D(multiplexer_1_out), .Q(A3), .reset(button_1_out));  // open: Qn, preset, en
  D_Flip_Flop #(.trigger("falling")) d_ff_2 (
    .clk(clock_1_out), .D(multiplexer_2_out), .Q(A2), .reset(button_1_out));  // open: Qn, preset, en
  D_Flip_Flop #(.trigger("falling")) d_ff_3 (
    .clk(clock_1_out), .D(multiplexer_3_out), .Q(A1), .reset(button_1_out));  // open: Qn, preset, en
  D_Flip_Flop #(.trigger("falling")) d_ff_4 (
    .clk(clock_1_out), .D(multiplexer_4_out), .Q(A0), .reset(button_1_out));  // open: Qn, preset, en
endmodule

module one (
  input  J,
  input  K,
  output Qn,
  output Qn_bar
);

  wire clock_1_out, n7400_1_p2, n7400_1_p4, n7400_2_p3, n7400_2_p9, n7404_1_p1, n7410_1_p2, n7410_1_p3;

  Clock clock_1 (.out(clock_1_out));
  // _7404 7404_1: pin names not known; wires that end beside it: n7404_1_p1, clock_1_out, 1'b1, 1'b0
  // _7410 7410_1: pin names not known; wires that end beside it: 1'b0, n7410_1_p2, n7410_1_p3, Qn, Qn_bar, clock_1_out, clock_1_out, K, J, 1'b1
  // _7400 7400_1: pin names not known; wires that end beside it: 1'b0, n7400_1_p2, n7410_1_p2, n7400_1_p4, n7400_1_p4, n7400_1_p2, n7410_1_p3, 1'b1
  // _7400 7400_2: pin names not known; wires that end beside it: 1'b0, Qn_bar, n7400_2_p3, n7400_2_p3, n7400_1_p2, Qn, n7404_1_p1, Qn, n7400_2_p9, Qn_bar, n7400_1_p4, n7400_2_p9, n7404_1_p1, 1'b1
endmodule

module two (
  input  PRESET,
  input  CLEAR,
  input  S1,
  input  S0,
  input  I3,
  input  I2,
  input  I1,
  input  I0,
  input  Right_Shift,
  input  Left_Shift,
  output A3,
  output A2,
  output A1,
  output A0
);

  wire CLOCK_out, n7404_1_p2, n7474_1_p8, n7474_1_p9, n7474_2_p8, n7474_2_p9;

  Clock CLOCK (.out(CLOCK_out));
  // _7404 7404_1: pin names not known; wires that end beside it: CLEAR, n7404_1_p2, 1'b0, 1'b1
  // _7474 7474_1: pin names not known; wires that end beside it: 1'b0, A2, A3, PRESET, PRESET, CLOCK_out, CLOCK_out, n7474_1_p8, n7474_1_p9, n7404_1_p2, n7404_1_p2, 1'b1
  // _74153 74153_1: pin names not known; wires that end beside it: 1'b0, n7474_1_p8, n7474_1_p9, A2, A3, A3, Right_Shift, A1, A2, I2, I3, S0, S1, 1'b0, 1'b0, 1'b1
  // _7474 7474_2: pin names not known; wires that end beside it: 1'b0, A0, A1, PRESET, PRESET, CLOCK_out, CLOCK_out, n7474_2_p8, n7474_2_p9, n7404_1_p2, n7404_1_p2, 1'b1
  // _74153 74153_2: pin names not known; wires that end beside it: 1'b0, n7474_2_p8, n7474_2_p9, A0, A1, A1, A2, Left_Shift, A0, I0, I1, S0, S1, 1'b0, 1'b0, 1'b1, S1, S0
endmodule
