// Logisim project online.circ as structural Verilog: 1 circuit, main circuit main
module main (
  input  PRESET,
  input  CLEAR,
  output Y1,
  output Y0,
  output Y2
);

  wire clock_1_out, JK_2_p5, JK_p3, JK_p7, JK_p10, NOT_p6;

  Clock clock_1 (.out(clock_1_out));
  // _7476 JK: pin names not known; wires that end beside it: clock_1_out, PRESET, JK_p3, 1'b1, clock_1_out, CLEAR, JK_p7, Y0, 1'b0, JK_p10, Y1, 1'b1
  // _7476 JK_2: pin names not known; wires that end beside it: clock_1_out, CLEAR, 1'b1, 1'b1, JK_2_p5, Y2, 1'b0
  // _7404 NOT: pin names not known; wires that end beside it: 1'b0, 1'b1, Y2, JK_p7, Y1, NOT_p6
  // _7432 OR: pin names not known; wires that end beside it: Y0, Y1, JK_2_p5, Y0, JK_p7, JK_p10, 1'b0, 1'b1, JK_p7, NOT_p6, JK_p3

  // Notes on the sheet:
  //   sequence: 1 -- 6 -- 2 -- 5 -- 3 -- 4 -- 7
endmodule
