// Logisim project one.circ as structural Verilog
module a (
  input  P,
  input  Q,
  input  R,
  output F
);

  wire and_1_out, and_2_out, not_1_out;

  not not_1 (not_1_out, Q);
  and and_1 (and_1_out, P, R);
  and and_2 (and_2_out, R, not_1_out);
  or or_1 (F, and_1_out, and_2_out);
endmodule

module b (
  input  P,
  input  Q,
  input  R,
  output F
);

  wire and_1_out, and_2_out, and_3_out, or_1_out;

  and and_1 (and_1_out, P, Q);
  and and_2 (and_2_out, Q, R);
  and and_3 (and_3_out, R, P);
  or or_1 (or_1_out, and_1_out, and_2_out);
  and and_4 (F, or_1_out, and_3_out);
endmodule

module c (
  input  P,
  input  Q,
  input  R,
  output F
);

  wire not_1_out;

  not not_1 (not_1_out, P);
  or or_1 (F, not_1_out, Q, R);
endmodule

module d (
  input  P,
  input  Q,
  input  R,
  output F
);

  wire AND_p3, AND_p6, NOT_p2;

  // _7404 NOT: pin names not known; wires that end beside it: Q, NOT_p2, 1'b0, 1'b1
  // _7408 AND: pin names not known; wires that end beside it: NOT_p2, R, AND_p3, P, R, AND_p6, 1'b0, 1'b1
  // _7432 AND_2: pin names not known; wires that end beside it: P, Q, R, AND_p3, AND_p6, F, 1'b0, 1'b1
endmodule

module e (
  input  P,
  input  Q,
  input  R,
  output F
);

  wire AND_p3, AND_p6, AND_p11, AND_p13;

  // _7408 AND: pin names not known; wires that end beside it: Q, R, AND_p3, P, Q, AND_p6, 1'b0, 1'b1, R, P, AND_p11, AND_p11, AND_p13, F
  // _7432 OR: pin names not known; wires that end beside it: P, Q, R, AND_p6, AND_p3, AND_p13, 1'b0, 1'b1
endmodule

module f (
  input  P,
  input  Q,
  input  R,
  output F
);

  wire NOT_p2, OR_p6;

  // _7404 NOT: pin names not known; wires that end beside it: P, NOT_p2, 1'b0, 1'b1
  // _7432 OR: pin names not known; wires that end beside it: P, Q, R, NOT_p2, Q, OR_p6, OR_p6, R, F, 1'b0, 1'b1
endmodule
