// Logisim project one.circ as structural Verilog
module XOR (
  input  A,
  input  B,
  output Y
);

  wire AND_p3, AND_p6, NOT_p2, NOT_p4;

  // _7404 NOT: pin names not known; wires that end beside it: B, NOT_p2, A, NOT_p4, 1'b0, 1'b1
  // _7408 AND: pin names not known; wires that end beside it: NOT_p2, A, AND_p3, NOT_p4, B, AND_p6, 1'b0, 1'b1
  // _7432 OR: pin names not known; wires that end beside it: A, B, AND_p3, AND_p6, Y, 1'b0, 1'b1
endmodule

module b (
  input  g2,
  input  g1,
  input  g0,
  output b2,
  output b1,
  output b0
);

  XOR xor_1 (.A(g1), .B(g2), .Y(b1));
  XOR xor_2 (.A(g0), .B(b1), .Y(b0));

  assign b2 = g2;

  // Notes on the sheet:
  //   b2 = g2
  //   b1 = g1 XOR b2
  //   b0 = g0 XOR b1
endmodule

module c (
  input  P,
  input  Q,
  input  R,
  input  S,
  output Y
);

  wire AND_p3, AND_p6;

  // _7432 AND: pin names not known; wires that end beside it: P, Q, AND_p3, R, S, AND_p6, 1'b0, 1'b1, 1'b1, 1'b0
  // _7408 OR: pin names not known; wires that end beside it: R, S, AND_p3, AND_p6, Y, 1'b0, 1'b1

  // Notes on the sheet:
  //   Y = (P+Q)(R+S)
endmodule

module a (
  input  P,
  input  Q,
  input  R,
  input  S,
  output F
);

  wire AND_p3, AND_p6, AND_p10, AND_p11, NOT_p2, OR_p5;

  // _7404 NOT: pin names not known; wires that end beside it: S, NOT_p2, 1'b0, 1'b1, 1'b1, 1'b0
  // _7408 AND: pin names not known; wires that end beside it: Q, R, AND_p3, AND_p3, NOT_p2, AND_p6, 1'b0, 1'b0, P, AND_p10, AND_p11
  // _7432 OR: pin names not known; wires that end beside it: S, NOT_p2, Q, R, OR_p5, OR_p5, NOT_p2, AND_p10, 1'b0, 1'b1, AND_p6, AND_p11, F

  // Notes on the sheet:
  //   F(P,Q,R,S) = P(Q+R+S') + QRS'
endmodule
