// Logisim project one.circ as structural Verilog
module b (
  input  V,
  input  W,
  input  X,
  input  Y,
  input  Z,
  output F
);

  wire AND_p2, AND_p3, AND_p8, AND_p11, n7404_1_p2, n7404_1_p4, n7404_1_p6;

  // _7404 7404_1: pin names not known; wires that end beside it: Y, n7404_1_p2, Z, n7404_1_p4, V, n7404_1_p6, 1'b0, 1'b1, 1'b1, 1'b0
  // _7408 AND: pin names not known; wires that end beside it: X, AND_p2, AND_p3, 1'b0, 1'b0, n7404_1_p6, n7404_1_p2, AND_p8, AND_p8, Z, AND_p11
  // _7432 OR: pin names not known; wires that end beside it: Z, n7404_1_p4, n7404_1_p2, n7404_1_p4, AND_p2, AND_p3, AND_p11, F, 1'b0, 1'b1

  // Notes on the sheet:
  //   F = X(Y'+Z') + V'Y'Z
endmodule

module a (
  input  A1,
  input  A0,
  input  B1,
  input  B0,
  output C2,
  output C1,
  output C0
);

  wire AND_p2, AND_p3, AND_p4, AND_p6, XOR_p7;

  // _7408 AND: pin names not known; wires that end beside it: 1'b0, AND_p2, AND_p3, AND_p4, A1, AND_p6, B1, AND_p6, B0, A0, 1'b1
  // _7432 OR: pin names not known; wires that end beside it: 1'b0, C2, AND_p4, AND_p3, A1, AND_p2, B1, 1'b1
  // _7486 XOR: pin names not known; wires that end beside it: 1'b0, C0, C1, A0, B1, B0, XOR_p7, XOR_p7, A1, AND_p6, 1'b1
endmodule
