// Logisim project one.circ as structural Verilog
module a (
  input  A,
  input  B,
  input  Bin,
  output C,
  output Bout
);

  wire AND_p3, NOT_p2, OR_p3, OR_p6, OR_p11, XOR_p5;

  // _7404 NOT: pin names not known; wires that end beside it: A, NOT_p2, 1'b0, 1'b1, 1'b1, 1'b0
  // _7408 OR: pin names not known; wires that end beside it: NOT_p2, Bin, OR_p3, NOT_p2, B, OR_p6, 1'b0, 1'b1, B, Bin, OR_p11
  // _7432 AND: pin names not known; wires that end beside it: OR_p3, OR_p6, AND_p3, AND_p3, OR_p11, Bout, 1'b1
  // _7486 XOR: pin names not known; wires that end beside it: Bin, 1'b0, A, B, XOR_p5, XOR_p5, Bin, C, 1'b0, 1'b1
endmodule

module b (
  input  A1,
  input  A0,
  input  B1,
  input  B0,
  output C2,
  output C1,
  output C0
);

  wire AND_2_p4, AND_2_p6, AND_2_p7, AND_2_p9, AND_2_p13, AND_p3, AND_p5, AND_p6, NOT_p2, NOT_p4, NOT_p6,
       NOT_p9, NOT_p10, NOT_p11, NOT_p12, XOR_p9;

  // _7404 NOT: pin names not known; wires that end beside it: A1, NOT_p2, A0, NOT_p4, B1, NOT_p6, 1'b1, B0, NOT_p9, NOT_p10, NOT_p11, NOT_p12, 1'b1, 1'b0
  // _7486 XOR: pin names not known; wires that end beside it: 1'b0, A1, B1, NOT_p10, A0, B0, NOT_p12, 1'b0, XOR_p9, 1'b1
  // _7408 AND: pin names not known; wires that end beside it: A0, NOT_p9, AND_p3, AND_p3, AND_p5, AND_p6, 1'b1, NOT_p11, XOR_p9, C1, A1, NOT_p6
  // _7408 AND_2: pin names not known; wires that end beside it: 1'b0, NOT_p4, B0, AND_2_p4, AND_2_p4, AND_2_p6, AND_2_p7, 1'b0, AND_2_p9, 1'b1, NOT_p2, B1, AND_2_p13
  // _7432 OR: pin names not known; wires that end beside it: A1, NOT_p6, AND_p5, NOT_p2, B1, AND_2_p6, 1'b1
  // _7432 OR_2: pin names not known; wires that end beside it: B1, NOT_p6, B0, NOT_p9, 1'b0, 1'b0, 1'b0, AND_2_p7, AND_2_p13, C0, AND_p6, AND_2_p9, C2

  // Notes on the sheet:
  //   A > B
  //   A = B
  //   A < B
endmodule
