// Logisim project one[fixed].circ as structural Verilog: 5 circuits, main circuit main
module main (
  input  X0,
  input  X1,
  input  X2,
  input  X3,
  output F
);

  wire n7404_1_p4, n7404_1_p6, n7404_1_p8, n7408_1_p4, n7408_1_p7, n7408_2_p5, n7432_1_p3, n7432_1_p6,
       n7432_1_p9, n7432_1_p10;

  // _7404 7404_1: pin names not known; wires that end beside it: 1'b0, 1'b1, 1'b0, n7404_1_p4, X2, n7404_1_p6, X1, n7404_1_p8, X3, 1'b1, n7404_1_p6, n7404_1_p4
  // _7408 7408_1: pin names not known; wires that end beside it: n7404_1_p8, n7404_1_p8, n7404_1_p6, n7408_1_p4, X3, X0, n7408_1_p7, 1'b0, 1'b1
  // _7432 7432_1: pin names not known; wires that end beside it: n7408_1_p4, n7408_1_p7, n7432_1_p3, n7404_1_p4, X1, n7432_1_p6, 1'b0, 1'b1, n7432_1_p9, n7432_1_p10, F
  // _7408 7408_2: pin names not known; wires that end beside it: X3, n7404_1_p8, n7404_1_p8, X0, n7408_2_p5, n7408_2_p5, n7432_1_p6, n7432_1_p9, 1'b0, 1'b1, n7432_1_p3, X2, n7432_1_p10
endmodule

module a (
  input  X0,
  input  X1,
  input  X2,
  input  X3,
  output F,
  output F_prime
);

  main main_1 (.X0(X0), .X1(X1), .X2(X2), .X3(X3), .F(F));
  not not_1 (F_prime, F);
endmodule

module b (
  input  [3:0] A,
  input  [3:0] B,
  output Output
);

  wire a_1_f, a_1_f_prime, a_2_f, a_2_f_prime, and_1_out, and_2_out;

  a a_1 (.X0(A[3]), .X1(A[2]), .X2(A[1]), .X3(A[0]), .F(a_1_f), .F_prime(a_1_f_prime));
  a a_2 (.X0(B[3]), .X1(B[2]), .X2(B[1]), .X3(B[0]), .F(a_2_f), .F_prime(a_2_f_prime));
  and and_1 (and_1_out, a_1_f_prime, a_2_f);
  and and_2 (and_2_out, a_2_f_prime, a_1_f);
  or or_1 (Output, and_1_out, and_2_out);

  // Notes on the sheet:
  //   F'(A)F(B) + F(A)F'(B)
endmodule

// C
module c (
  input  x0,
  input  x1,
  input  x2,
  input  x3,
  output F,
  output F_prime
);

  main main_1 (.X0(x0), .X1(x1), .X2(x2), .X3(x3), .F(F));
  // _7404 7404_1: pin names not known; wires that end beside it: 1'b1, F, F_prime, 1'b0, 1'b1
endmodule

module d (
  input  [3:0] A,
  input  [3:0] B,
  output Output
);

  wire c_1_f, c_1_f_prime, c_2_f, c_2_f_prime, n7408_1_p3, n7408_1_p6;

  c c_1 (.x0(A[3]), .x1(A[2]), .x2(A[1]), .x3(A[0]), .F(c_1_f), .F_prime(c_1_f_prime));
  c c_2 (.x0(B[3]), .x1(B[2]), .x2(B[1]), .x3(B[0]), .F(c_2_f), .F_prime(c_2_f_prime));
  // _7408 7408_1: pin names not known; wires that end beside it: c_1_f_prime, c_2_f, n7408_1_p3, c_1_f, c_2_f_prime, n7408_1_p6, 1'b1
  // _7432 7432_1: pin names not known; wires that end beside it: 1'b0, n7408_1_p3, n7408_1_p6, Output, 1'b0, 1'b1

  // Notes on the sheet:
  //   F'(A)F(B) + F(A)F'(B)
endmodule
