// Logisim project one.circ as structural Verilog
module a (
  input  P,
  input  Q,
  input  R,
  input  S,
  output F
);

  wire AND1_p3, AND1_p6, AND1_p10, NOT_p2, OR_p3, OR_p4, OR_p6, OR_p7;

  // _7404 NOT: pin names not known; wires that end beside it: S, NOT_p2, 1'b0, 1'b1
  // _7408 AND1: pin names not known; wires that end beside it: NOT_p2, R, AND1_p3, AND1_p3, Q, AND1_p6, 1'b1, NOT_p2, P, AND1_p10
  // _7432 OR: pin names not known; wires that end beside it: 1'b0, AND1_p6, OR_p3, OR_p4, OR_p4, OR_p6, OR_p7, 1'b1, AND1_p10, OR_p7, F
  // _7408 AND2: pin names not known; wires that end beside it: Q, R, S, 1'b0, P, R, OR_p3, P, Q, OR_p6, 1'b0, 1'b1
endmodule
