// Logisim project online.circ as structural Verilog: 1 circuit, main circuit main
module main (
  input  A3,
  input  A2,
  input  A1,
  input  A0,
  output F
);

  wire n7408_1_p3, n7408_1_p6, n7408_1_p10, n74138_1_p7, n74138_1_p10, n74138_2_p9, n74138_2_p10,
       n74138_2_p11;

  // _74138 74138_1: pin names not known; wires that end beside it: A0, A1, A2, A3, 1'b0, 1'b1, n74138_1_p7, 1'b0, 1'b1, n74138_1_p10
  // _74138 74138_2: pin names not known; wires that end beside it: A0, A1, A2, 1'b0, 1'b0, A3, 1'b0, 1'b1, n74138_2_p9, n74138_2_p10, n74138_2_p11
  // _7408 7408_1: pin names not known; wires that end beside it: n74138_1_p10, n74138_1_p7, n7408_1_p3, n7408_1_p3, n74138_2_p9, n7408_1_p6, 1'b0, 1'b1, n74138_2_p11, n7408_1_p10, F, n74138_2_p10, n7408_1_p6, n7408_1_p10

  // Notes on the sheet:
  //   Implementation of a given boolean function F by 2 3*8 decoder
  //   F = Product(6,7,8,9,10)
endmodule
