// Logisim project online.circ as structural Verilog: 1 circuit, main circuit main
module main (
  input  A,
  input  B,
  input  C,
  input  D,
  output f
);

  wire n7404_1_p2, n7432_1_p3;

  // _7404 7404_1: pin names not known; wires that end beside it: D, n7404_1_p2, 1'b0, 1'b1, 1'b1, 1'b0
  // _7432 7432_1: pin names not known; wires that end beside it: C, D, n7432_1_p3, 1'b0, 1'b1
  // _74153 74153_1: pin names not known; wires that end beside it: 1'b0, A, n7404_1_p2, 1'b0, n7432_1_p3, C, f, 1'b0, 1'b1, 1'b0, B

  // Notes on the sheet:
  //   f = SUMMATION(2, 3, 5, 6, 7, 12, 14)
endmodule
